// Logisim project ALU_prototype.circ as structural Verilog: 2 circuits, main circuit ALU
module ALU (
  input  [15:0] SideA,
  input  [15:0] SideB,
  input  CarryIn,
  input  [3:0] FuncControl,
  output [15:0] AluResult,
  output ZeroOut,
  output CarryOut
);

  wire adder_1_cout, multiplexer_1_out, not_1_out;
  wire [15:0] adder_1_out, multiplexer_2_out, not_2_out, SideA_AND_SideB_out, SideA_NOT_out,
       SideA_OR_SideB_out, SideA_XOR_SideB_out, SideB_Enable_out;

  assign SideB_Enable_out = SideB & {16{1'b1}};  // AND_Gate SideB_Enable, 16 bits wide
  assign SideA_NOT_out = ~SideA;  // NOT_Gate SideA_NOT, 16 bits wide
  not not_1 (not_1_out, CarryIn);
  assign not_2_out = ~SideB_Enable_out;  // NOT_Gate not_2, 16 bits wide
  Multiplexer multiplexer_1 (.in0(CarryIn), .in1(not_1_out), .out(multiplexer_1_out), .sel(FuncControl[0]));
  Multiplexer #(.width(16)) multiplexer_2 (
    .in0(SideB_Enable_out), .in1(not_2_out), .out(multiplexer_2_out), .sel(FuncControl[0]));
  assign SideA_AND_SideB_out = SideA & SideB_Enable_out;  // AND_Gate SideA_AND_SideB, 16 bits wide
  assign SideA_OR_SideB_out = SideA | SideB_Enable_out;  // OR_Gate SideA_OR_SideB, 16 bits wide
  assign SideA_XOR_SideB_out = SideA ^ SideB_Enable_out;  // XOR_Gate SideA_XOR_SideB, 16 bits wide
  Adder #(.width(16)) adder_1 (
    .a(SideA), .b(multiplexer_2_out), .out(adder_1_out), .cin(multiplexer_1_out), .cout(adder_1_cout));
  Multiplexer #(.select(4), .width(16)) multiplexer_3 (
    .in0(SideA), .in1(SideB_Enable_out), .in2(SideA_AND_SideB_out), .in3(SideA_OR_SideB_out),
    .in4(SideA_XOR_SideB_out), .in5(SideA_NOT_out), .in6({SideA[14:0], CarryIn}),
    .in7({CarryIn, SideA[15:1]}), .in8(adder_1_out), .in9(adder_1_out), .in10(adder_1_out),
    .in11(adder_1_out), .in12(adder_1_out), .in13(adder_1_out), .in14(adder_1_out), .in15(adder_1_out),
    .out(AluResult), .sel(FuncControl));
  Multiplexer #(.select(2)) multiplexer_4 (
    .in0(SideA[15]), .in1(SideA[0]), .in2(adder_1_cout), .in3(adder_1_cout), .out(CarryOut),
    .sel({FuncControl[3], FuncControl[0]}));
  nor nor_1 (ZeroOut, AluResult[0], AluResult[1], AluResult[2], AluResult[3], AluResult[4], AluResult[5], AluResult[6], AluResult[7], AluResult[8], AluResult[9], AluResult[10], AluResult[11], AluResult[12], AluResult[13], AluResult[14], AluResult[15]);
endmodule

module Datapath (
  input  SelPC
);

  wire undriven;
  wire [2:0] RegFile_q, RegSelRa_q, RegSelRb_q;
  wire [15:0] alu_1_aluresult, demultiplexer_1_out0, demultiplexer_1_out1, demultiplexer_1_out2,
       demultiplexer_1_out3, demultiplexer_1_out4, demultiplexer_1_out5, demultiplexer_1_out6,
       demultiplexer_1_out7, multiplexer_1_out, multiplexer_2_out, multiplexer_3_out, multiplexer_4_out,
       multiplexer_5_out, multiplexer_6_out, ram_1_dout, register_1_q, register_2_q, register_3_q,
       register_4_q, register_5_q, register_6_q, register_7_q, register_8_q, RegPC_q, RegTmpRa_q, RegTmpRb_q;

  Multiplexer #(.width(16)) multiplexer_1 (
    .in0(alu_1_aluresult), .in1(multiplexer_4_out), .out(multiplexer_1_out), .sel(SelPC));
  Multiplexer #(.width(16)) multiplexer_2 (.in0(RegPC_q), .in1(RegTmpRb_q), .out(multiplexer_2_out));  // open: sel
  RAM #(.addrWidth(16), .dataWidth(16)) ram_1 (
    .addr(multiplexer_2_out), .din(RegTmpRa_q), .dout(ram_1_dout));  // open: we, oe, clk
  Register #(.width(16)) RegPC (.D(multiplexer_1_out), .Q(RegPC_q));  // open: en, clk, clr
  Register #(.width(3)) RegFile (.Q(RegFile_q));  // open: D, en, clk, clr
  Multiplexer #(.width(16)) multiplexer_3 (
    .in0(alu_1_aluresult), .in1(ram_1_dout), .out(multiplexer_3_out));  // open: sel
  Demultiplexer #(.select(3), .width(16)) demultiplexer_1 (
    .out0(demultiplexer_1_out0), .out1(demultiplexer_1_out1), .out2(demultiplexer_1_out2),
    .out3(demultiplexer_1_out3), .out4(demultiplexer_1_out4), .out5(demultiplexer_1_out5),
    .out6(demultiplexer_1_out6), .out7(demultiplexer_1_out7), .in(multiplexer_3_out), .sel(RegFile_q));
  Register #(.width(16)) register_1 (.D(demultiplexer_1_out0), .Q(register_1_q));  // open: en, clk, clr
  Register #(.width(16)) register_2 (.D(demultiplexer_1_out1), .Q(register_2_q));  // open: en, clk, clr
  Register #(.width(16)) register_3 (.D(demultiplexer_1_out2), .Q(register_3_q));  // open: en, clk, clr
  Register #(.width(16)) register_4 (.D(demultiplexer_1_out3), .Q(register_4_q));  // open: en, clk, clr
  Register #(.width(16)) register_5 (.D(demultiplexer_1_out4), .Q(register_5_q));  // open: en, clk, clr
  Register #(.width(16)) register_6 (.D(demultiplexer_1_out5), .Q(register_6_q));  // open: en, clk, clr
  Register #(.width(16)) register_7 (.D(demultiplexer_1_out6), .Q(register_7_q));  // open: en, clk, clr
  Register #(.width(16)) register_8 (.D(demultiplexer_1_out7), .Q(register_8_q));  // open: en, clk, clr
  Register #(.width(3)) RegSelRa (.Q(RegSelRa_q));  // open: D, en, clk, clr
  Multiplexer #(.select(3), .width(16)) multiplexer_4 (
    .in0(register_1_q), .in1(register_2_q), .in2(register_3_q), .in3(register_4_q), .in4(register_5_q),
    .in5(register_6_q), .in6(register_7_q), .in7(register_8_q), .out(multiplexer_4_out), .sel(RegSelRa_q));
  Register #(.width(3)) RegSelRb (.Q(RegSelRb_q));  // open: D, en, clk, clr
  Multiplexer #(.select(3), .width(16)) multiplexer_5 (
    .in0(register_1_q), .in1(register_2_q), .in2(register_3_q), .in3(register_4_q), .in4(register_5_q),
    .in5(register_6_q), .in6(register_7_q), .in7(register_8_q), .out(multiplexer_5_out), .sel(RegSelRb_q));
  Register #(.width(16)) RegTmpRa (.D(multiplexer_4_out), .Q(RegTmpRa_q), .clr(undriven));  // open: en, clk
  Register #(.width(16)) RegTmpRb (.D(multiplexer_5_out), .Q(RegTmpRb_q));  // open: en, clk, clr
  Multiplexer #(.width(16)) multiplexer_6 (.in0(RegTmpRa_q), .in1(RegPC_q), .out(multiplexer_6_out), .sel(SelPC));
  ALU alu_1 (
    .SideA(multiplexer_6_out), .SideB(RegTmpRb_q), .AluResult(alu_1_aluresult));  // open: CarryIn, FuncControl, ZeroOut, CarryOut
endmodule
